# Fritzing sketch circuito (saved by Fritzing 0.9.5d)
breadboards: 1

parts:
  U1 = NodeMCU V3.0  # not connected
  Q1 = NPN-Transistor [package="TO92 [THT]"]
  LED1 = LED - 5mm [color="Infrared (940nm)" package="5 mm [THT]"]
  IR1 = vs1838b [package=THT]

nets:
  N1: Q1.E, IR1.GND
  N2: Q1.C, LED1.cathode
  N3: LED1.anode, IR1.Vs

custom parts:
  NodeMCU V3.0: ESP8266 based NodeMCU
